# Fritzing sketch Drone-Remote (saved by Fritzing 0.9.3b)
breadboards: 1

parts:
  Bauteil1 = Arduino Pro Mini v13
  Bauteil2 = Adafruit RFM9x LoRa Radio [part_number="Adafruit #3072 and #3073"]
  ANT1 = Antenna
  U1 = Voltage Regulator -- 3.3 V -- LM1117
  U2 = LIPO-110mAh [package=lipo-110]
  LCD1 = LCD screen
  U3 = 74HC595 [package="DIP16 [THT]"]  # not connected

nets:
  GND: Bauteil1.GND, Bauteil2.GND, U1.GND, U2.-, LCD1.VSS, LCD1.R/W, LCD1.LED-
  VCC: Bauteil1.VCC, Bauteil2.VIN, U1.OUT, LCD1.VDD, LCD1.LED+
  N1: Bauteil1.A0, U1.IN, U2.+
  N2: Bauteil1.D13/SCK, Bauteil2.SCK
  N3: Bauteil1.D12/MISO, Bauteil2.MISO
  N4: Bauteil1.D11_PWM/MOSI, Bauteil2.MOSI
  N5: Bauteil1.D10_PWM/SS, Bauteil2.CS
  N6: Bauteil1.D8, LCD1.RS
  N7: Bauteil1.D7, LCD1.E
  N8: Bauteil1.D5_PWM, LCD1.DB4
  N9: Bauteil1.D4, LCD1.DB5
  N10: Bauteil1.D3_PWM, LCD1.DB6
  N11: Bauteil1.D2, LCD1.DB7
  N12: Bauteil2.ANTENNA, ANT1.antenna_lead

custom parts:
  Adafruit RFM9x LoRa Radio: Sending data over long distances is like magic, and now you can be a magician with this range of powerful and easy-to-use radio modules. Sure, sometimes you want to talk to a computer (a good time to use WiFi) or perhaps communicate with a Phone (choose Bluetooth Low Energy!) but what if you want to send data very far? Most WiFi, Bluetooth, Zigbee and other wireless chipsets use 2.4GHz, which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
  Voltage Regulator -- 3.3 V -- LM1117: LM1117-3.3 Voltage regulator, 3.3 V output. Note that the pinout order is not the same as LM7805 or LM7833.
