# Fritzing sketch Drone-Schematic (saved by Fritzing 0.9.3b)
breadboards: 1

parts:
  Q1 = NPN-Transistor [package="TO92 [THT]"]
  R1 = Resistor [tolerance=±5% resistance=6.5 package=THT]
  R2 = Resistor [tolerance=±5% resistance=47 package=THT]
  Arduino_Pro_Mini_3_3V = Arduino Pro Mini v13
  U1 = LIPO-110mAh [package=lipo-110]
  Q2 = NPN-Transistor [package="TO92 [THT]"]
  R3 = Resistor [tolerance=±5% resistance=6.5 package=THT]
  R4 = Resistor [tolerance=±5% resistance=47 package=THT]
  Q3 = NPN-Transistor [package="TO92 [THT]"]
  R5 = Resistor [tolerance=±5% resistance=6.5 package=THT]
  R6 = Resistor [tolerance=±5% resistance=47 package=THT]
  Q4 = NPN-Transistor [package="TO92 [THT]"]
  R7 = Resistor [tolerance=±5% resistance=6.5 package=THT]
  R8 = Resistor [tolerance=±5% resistance=47 package=THT]
  C1 = Electrolytic Capacitor [capacitance=10µF package="100 mil [THT, electrolytic]"]
  C2 = Electrolytic Capacitor [capacitance=10µF package="100 mil [THT, electrolytic]"]
  C3 = Electrolytic Capacitor [capacitance=10µF package="100 mil [THT, electrolytic]"]
  C4 = Electrolytic Capacitor [capacitance=10µF package="100 mil [THT, electrolytic]"]
  C5 = Electrolytic Capacitor [capacitance=220µF package="100 mil [THT, electrolytic]"]
  3-Axis_Accelerometer1 = 3-Axis Accelerometer Breakout - MMA8452Q
  RFM95 = Adafruit RFM9x LoRa Radio [part_number="Adafruit #3072 and #3073"]
  ANT1 = Antenna
  LED1 = LED - 3mm [color="Red (633nm)" package="3 mm [THT]"]
  R9 = Resistor [tolerance=±5% resistance=220 package=THT]
  U2 = Voltage Regulator -- 3.3 V -- LM1117

nets:
  N1: Q1.E, R1.Pin_1, Arduino_Pro_Mini_3_3V.A0, C1.+
  N2: Q1.B, R2.Pin_1
  N3: Q1.C, U1.+, Q2.C, Q3.C, Q4.C, C5.+, U2.IN
  N4: R1.Pin_0, R3.Pin_0, R5.Pin_0, R7.Pin_0, C1.-, C2.-, C3.-, C4.-, C5.-
  N5: R2.Pin_0, Arduino_Pro_Mini_3_3V.D3_PWM
  VCC: Arduino_Pro_Mini_3_3V.VCC, 3-Axis_Accelerometer1.3.3V, RFM95.VIN, U2.OUT
  GND: Arduino_Pro_Mini_3_3V.GND, U1.-, 3-Axis_Accelerometer1.GND, RFM95.GND, LED1.cathode, U2.GND
  N6: Arduino_Pro_Mini_3_3V.A4, 3-Axis_Accelerometer1.SDA
  N7: Arduino_Pro_Mini_3_3V.A5, 3-Axis_Accelerometer1.SCL
  N8: Arduino_Pro_Mini_3_3V.A3, Q4.E, R7.Pin_1, C4.+
  N9: Arduino_Pro_Mini_3_3V.A2, Q3.E, R5.Pin_1, C3.+
  N10: Arduino_Pro_Mini_3_3V.A1, Q2.E, R3.Pin_1, C2.+
  N11: Arduino_Pro_Mini_3_3V.D13/SCK, RFM95.SCK
  N12: Arduino_Pro_Mini_3_3V.D12/MISO, RFM95.MISO
  N13: Arduino_Pro_Mini_3_3V.D11_PWM/MOSI, RFM95.MOSI
  N14: Arduino_Pro_Mini_3_3V.D10_PWM/SS, RFM95.CS
  N15: Arduino_Pro_Mini_3_3V.D9_PWM, R8.Pin_0
  N16: Arduino_Pro_Mini_3_3V.D8, RFM95.DIO0
  N17: Arduino_Pro_Mini_3_3V.D7, RFM95.RST
  N18: Arduino_Pro_Mini_3_3V.D6_PWM, R6.Pin_0
  N19: Arduino_Pro_Mini_3_3V.D5_PWM, R4.Pin_0
  N20: Arduino_Pro_Mini_3_3V.D4, RFM95.DIO1
  N21: Arduino_Pro_Mini_3_3V.D2, R9.Pin_0
  N22: Q2.B, R4.Pin_1
  N23: Q3.B, R6.Pin_1
  N24: Q4.B, R8.Pin_1
  N25: RFM95.ANTENNA, ANT1.antenna_lead
  N26: LED1.anode, R9.Pin_1

custom parts:
  Adafruit RFM9x LoRa Radio: Sending data over long distances is like magic, and now you can be a magician with this range of powerful and easy-to-use radio modules. Sure, sometimes you want to talk to a computer (a good time to use WiFi) or perhaps communicate with a Phone (choose Bluetooth Low Energy!) but what if you want to send data very far? Most WiFi, Bluetooth, Zigbee and other wireless chipsets use 2.4GHz, which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
  Voltage Regulator -- 3.3 V -- LM1117: LM1117-3.3 Voltage regulator, 3.3 V output. Note that the pinout order is not the same as LM7805 or LM7833.
