# Fritzing sketch Remote-Schematic (saved by Fritzing 0.9.3b)
breadboards: 1

parts:
  Bauteil1 = Arduino Pro Mini v13
  Bauteil2 = Adafruit RFM9x LoRa Radio [part_number="Adafruit #3072 and #3073"]
  ANT1 = Antenna
  U1 = Voltage Regulator -- 3.3 V -- LM1117
  U2 = LIPO-110mAh [package=lipo-110]
  PS2-Controller_1 = IC, SIP package, 9 pins [chip_label=PS2-Controller]
  R1 = Resistor [tolerance=±5% resistance=1k package=THT]
  R2 = Resistor [tolerance=±5% resistance=1k package=THT]
  R3 = Resistor [tolerance=±5% resistance=220k package=THT]
  R4 = Resistor [tolerance=±5% resistance=220k package=THT]

nets:
  GND: Bauteil1.GND, Bauteil2.GND, U1.GND, U2.-, PS2-Controller_1.pin4, R3.Pin_1
  VCC: Bauteil1.VCC, Bauteil2.VIN, U1.OUT, PS2-Controller_1.pin5, R1.Pin_0, R2.Pin_0
  N1: Bauteil1.A0, R3.Pin_0, R4.Pin_1
  N2: Bauteil1.D13/SCK, Bauteil2.SCK, PS2-Controller_1.pin7
  N3: Bauteil1.D12/MISO, Bauteil2.MISO, PS2-Controller_1.pin1, R1.Pin_1
  N4: Bauteil1.D11_PWM/MOSI, Bauteil2.MOSI, PS2-Controller_1.pin2
  N5: Bauteil1.D9_PWM, PS2-Controller_1.pin6, R2.Pin_1
  N6: Bauteil1.D8, Bauteil2.CS
  N7: Bauteil1.D7, Bauteil2.DIO0
  N8: Bauteil1.D6_PWM, Bauteil2.DIO1
  N9: Bauteil1.D4, Bauteil2.RST
  N10: Bauteil2.ANTENNA, ANT1.antenna_lead
  N11: U1.IN, U2.+, R4.Pin_0

custom parts:
  Adafruit RFM9x LoRa Radio: Sending data over long distances is like magic, and now you can be a magician with this range of powerful and easy-to-use radio modules. Sure, sometimes you want to talk to a computer (a good time to use WiFi) or perhaps communicate with a Phone (choose Bluetooth Low Energy!) but what if you want to send data very far? Most WiFi, Bluetooth, Zigbee and other wireless chipsets use 2.4GHz, which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
  Voltage Regulator -- 3.3 V -- LM1117: LM1117-3.3 Voltage regulator, 3.3 V output. Note that the pinout order is not the same as LM7805 or LM7833.
