# Fritzing sketch Drone-Schematic (saved by Fritzing 0.9.3b)
breadboards: 1

parts:
  Q1 = NPN-Transistor [package="TO92 [THT]"]
  R1 = Resistor [tolerance=±5% resistance=6.5 package=THT]
  R2 = Resistor [tolerance=±5% resistance=47 package=THT]
  U1 = LIPO-110mAh [package=lipo-110]
  Q2 = NPN-Transistor [package="TO92 [THT]"]
  R3 = Resistor [tolerance=±5% resistance=6.5 package=THT]
  R4 = Resistor [tolerance=±5% resistance=47 package=THT]
  Q3 = NPN-Transistor [package="TO92 [THT]"]
  R5 = Resistor [tolerance=±5% resistance=6.5 package=THT]
  R6 = Resistor [tolerance=±5% resistance=47 package=THT]
  Q4 = NPN-Transistor [package="TO92 [THT]"]
  R7 = Resistor [tolerance=±5% resistance=6.5 package=THT]
  R8 = Resistor [tolerance=±5% resistance=47 package=THT]
  C1 = Electrolytic Capacitor [capacitance=10µF package="100 mil [THT, electrolytic]"]
  C2 = Electrolytic Capacitor [capacitance=10µF package="100 mil [THT, electrolytic]"]
  C3 = Electrolytic Capacitor [capacitance=10µF package="100 mil [THT, electrolytic]"]
  C4 = Electrolytic Capacitor [capacitance=10µF package="100 mil [THT, electrolytic]"]
  C5 = Electrolytic Capacitor [capacitance=220µF package="100 mil [THT, electrolytic]"]
  3-Axis_Accelerometer1 = 3-Axis Accelerometer Breakout - MMA8452Q
  RFM95 = Adafruit RFM9x LoRa Radio [part_number="Adafruit #3072 and #3073"]
  ANT1 = Antenna
  LED1 = LED - 3mm [color="Red (633nm)" package="3 mm [THT]"]
  R9 = Resistor [tolerance=±5% resistance=220 package=THT]
  R10 = Resistor [tolerance=±5% resistance=220k package=THT]
  R11 = Resistor [tolerance=±5% resistance=220k package=THT]
  IC1 = Voltage Regulator AMS1117 [package=sot223]
  Arduino_Pro_Mini_5V/16MHz_v14 = Arduino Pro Mini (5V)
  Bauteil1 = USB LiPoly Charger
  Bauteil2 = NCP1400 Step-Up Breakout

nets:
  N1: Q1.E, R1.Pin_1, C1.+, Arduino_Pro_Mini_5V/16MHz_v14.A0
  N2: Q1.B, R2.Pin_1
  N3: Q1.C, U1.+, Q2.C, Q3.C, Q4.C, C5.+, R11.Pin_0, Bauteil1.VBAT, Bauteil2.VIN
  GND: R1.Pin_0, U1.-, R3.Pin_0, R5.Pin_0, R7.Pin_0, C1.-, C2.-, C3.-, C4.-, C5.-, 3-Axis_Accelerometer1.GND, RFM95.GND, LED1.cathode, R10.Pin_0, IC1.GND, Arduino_Pro_Mini_5V/16MHz_v14.GND, Bauteil1.GND, Bauteil2.GND
  N4: R2.Pin_0, Arduino_Pro_Mini_5V/16MHz_v14.D3
  N5: Q2.E, R3.Pin_1, C2.+, Arduino_Pro_Mini_5V/16MHz_v14.A1
  N6: Q2.B, R4.Pin_1
  N7: R4.Pin_0, Arduino_Pro_Mini_5V/16MHz_v14.D5
  N8: Q3.E, R5.Pin_1, C3.+, Arduino_Pro_Mini_5V/16MHz_v14.A2
  N9: Q3.B, R6.Pin_1
  N10: R6.Pin_0, Arduino_Pro_Mini_5V/16MHz_v14.D6
  N11: Q4.E, R7.Pin_1, C4.+, Arduino_Pro_Mini_5V/16MHz_v14.A3
  N12: Q4.B, R8.Pin_1
  N13: R8.Pin_0, Arduino_Pro_Mini_5V/16MHz_v14.D9
  3.3V: 3-Axis_Accelerometer1.3.3V, RFM95.VIN, IC1.OUT
  N14: 3-Axis_Accelerometer1.SDA, Arduino_Pro_Mini_5V/16MHz_v14.A4
  N15: 3-Axis_Accelerometer1.SCL, Arduino_Pro_Mini_5V/16MHz_v14.A5
  N16: RFM95.DIO1, Arduino_Pro_Mini_5V/16MHz_v14.D4
  N17: RFM95.ANTENNA, ANT1.antenna_lead
  N18: RFM95.DIO0, Arduino_Pro_Mini_5V/16MHz_v14.D10
  N19: RFM95.SCK, Arduino_Pro_Mini_5V/16MHz_v14.SCK
  N20: RFM95.MISO, Arduino_Pro_Mini_5V/16MHz_v14.MISO
  N21: RFM95.MOSI, Arduino_Pro_Mini_5V/16MHz_v14.MOSI
  N22: RFM95.CS, Arduino_Pro_Mini_5V/16MHz_v14.D8
  N23: RFM95.RST, Arduino_Pro_Mini_5V/16MHz_v14.D7
  N24: LED1.anode, R9.Pin_1
  N25: R9.Pin_0, Arduino_Pro_Mini_5V/16MHz_v14.D2
  N26: R10.Pin_1, R11.Pin_1, Arduino_Pro_Mini_5V/16MHz_v14.A6
  N27: IC1.IN, Arduino_Pro_Mini_5V/16MHz_v14.VCC, Bauteil2.VOUT

custom parts:
  Adafruit RFM9x LoRa Radio: Sending data over long distances is like magic, and now you can be a magician with this range of powerful and easy-to-use radio modules. Sure, sometimes you want to talk to a computer (a good time to use WiFi) or perhaps communicate with a Phone (choose Bluetooth Low Energy!) but what if you want to send data very far? Most WiFi, Bluetooth, Zigbee and other wireless chipsets use 2.4GHz, which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
