# Fritzing sketch Remote-Schematic (saved by Fritzing 0.9.3b)
breadboards: 1

parts:
  RFM95 = Adafruit RFM9x LoRa Radio [part_number="Adafruit #3072 and #3073"]
  ANT1 = Antenna
  U2 = LIPO-110mAh [package=lipo-110]
  PS2-Controller_1 = IC, SIP package, 9 pins [chip_label=PS2-Controller]
  R1 = Resistor [tolerance=±5% resistance=1k package=THT]
  R2 = Resistor [tolerance=±5% resistance=1k package=THT]
  R3 = Resistor [tolerance=±5% resistance=220k package=THT]
  R4 = Resistor [tolerance=±5% resistance=220k package=THT]
  IC1 = Voltage Regulator AMS1117 [package=sot223]
  Arduino_Pro_Mini_3_3V/8MHz_v14 = Arduino Pro Mini (3.3V)

nets:
  N1: RFM95.DIO1, Arduino_Pro_Mini_3_3V/8MHz_v14.D6
  N2: RFM95.ANTENNA, ANT1.antenna_lead
  VIN: RFM95.VIN, PS2-Controller_1.pin5, R1.Pin_0, R2.Pin_0, IC1.OUT, Arduino_Pro_Mini_3_3V/8MHz_v14.VCC
  GND: RFM95.GND, U2.-, PS2-Controller_1.pin4, R3.Pin_1, IC1.GND, Arduino_Pro_Mini_3_3V/8MHz_v14.GND
  N3: RFM95.DIO0, Arduino_Pro_Mini_3_3V/8MHz_v14.D5
  N4: RFM95.SCK, PS2-Controller_1.pin7, Arduino_Pro_Mini_3_3V/8MHz_v14.SCK
  N5: RFM95.MISO, PS2-Controller_1.pin1, R1.Pin_1, Arduino_Pro_Mini_3_3V/8MHz_v14.MISO
  N6: RFM95.MOSI, PS2-Controller_1.pin2, Arduino_Pro_Mini_3_3V/8MHz_v14.MOSI
  N7: RFM95.CS, Arduino_Pro_Mini_3_3V/8MHz_v14.D7
  N8: RFM95.RST, Arduino_Pro_Mini_3_3V/8MHz_v14.D4
  N9: U2.+, R4.Pin_0, IC1.IN
  N10: PS2-Controller_1.pin6, R2.Pin_1, Arduino_Pro_Mini_3_3V/8MHz_v14.D8
  N11: R3.Pin_0, R4.Pin_1, Arduino_Pro_Mini_3_3V/8MHz_v14.A0

custom parts:
  Adafruit RFM9x LoRa Radio: Sending data over long distances is like magic, and now you can be a magician with this range of powerful and easy-to-use radio modules. Sure, sometimes you want to talk to a computer (a good time to use WiFi) or perhaps communicate with a Phone (choose Bluetooth Low Energy!) but what if you want to send data very far? Most WiFi, Bluetooth, Zigbee and other wireless chipsets use 2.4GHz, which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
